# Fritzing sketch interrupts (saved by Fritzing 0.5.2b)
breadboards: 1

parts:
  R1 = Resistor [resistance=10k package=THT]
  Arduino1 = Arduino
  S1 = Pushbutton [package="[THT]"]
  R2 = Resistor [resistance=220 package=THT]

nets:
  N1: R1.Pin_0, Arduino1.GND, S1.Pin_1, S1.Pin_2
  N2: R1.Pin_1, Arduino1.D12
  N3: Arduino1.D2, S1.Pin_3, S1.Pin_4, R2.Pin_1
  N4: Arduino1.+5V, R2.Pin_0

notes:
  attach ground to PIN12 with a resistor
  RED = +5V
  BLACK = Ground
  Interrupt 0 -> Digital PIN 2
