# Fritzing sketch lm35 (saved by Fritzing 0.5.2b)
breadboards: 1

parts:
  R1 = Resistor [resistance=10k package=THT]
  Arduino1 = Arduino Mega
  Q1 = PNP-Transistor [package="TO92 [THT]"]
  R2 = Resistor [resistance=10k package=THT]

nets:
  N1: R1.Pin_0, Arduino1.GND
  N2: R1.Pin_1, Arduino1.D13
  N3: Arduino1.A0, Q1.B, R2.Pin_0
  N4: Q1.C, R2.Pin_1

notes:
  attach ground to PIN13 with a resistor
  RED = +5V
  BLACK = Ground
  This is a LM35 ----->
