# Fritzing sketch ubuntu-workaround (saved by Fritzing 0.5.2b)

parts:
  Arduino1 = Arduino
  R1 = Resistor [resistance=10k package=THT]

nets:
  N1: Arduino1.GND, R1.Pin_0
  N2: Arduino1.D12, R1.Pin_1

notes:
  10k R - Ground to pin 12
